# Fritzing sketch Doorbell Sketch (saved by Fritzing 0.9.3b)
breadboards: 1

parts:
  Part1 = Arduino Uno (Rev3)
  SPKR1 = Loudspeaker
  LED1 = LED - 5mm [color="Red (633nm)" package="5 mm [THT]"]
  LED2 = LED - 5mm [color="Blue (470nm)" package="5 mm [THT]"]
  LED3 = LED - 5mm [color="Green (555nm)" package="5 mm [THT]"]
  R1 = Resistor [tolerance=±5% resistance=220 package=THT]
  S1 = Pushbutton [package="[THT]"]

nets:
  N1: Part1.D9_PWM, LED3.anode
  N2: Part1.D10_PWM/SS, LED2.anode
  N3: Part1.D11_PWM/MOSI, LED1.anode
  N4: Part1.D12/MISO, S1.Pin_1, S1.Pin_2
  N5: Part1.5V, S1.Pin_3, S1.Pin_4
  N6: Part1.GND, SPKR1.pin1, R1.Pin_0
  N7: LED1.cathode, LED2.cathode, LED3.cathode, R1.Pin_1
